// Logisim project 16 bit alu.circ as structural Verilog: 3 circuits, main circuit main
module main (
  input  Carry_In,
  input  [15:0] Operand_A,
  input  [15:0] Operand_B,
  input  [1:0] Operation,
  input  Binvert,
  output zero,
  output [15:0] result,
  output carry15,
  output overflow
);

  _16_bit_ALU u_16_bit_alu_1 (
    .Operand_A(Operand_A), .Operand_B(Operand_B), .Operation(Operation), .Binvert(Binvert), .result(result),
    .Carry15(carry15), .Carry_In(Carry_In), .Overflow(overflow), .zero(zero));
endmodule

// ALU 0
module _1_Bit_ALU (
  input  Operand_B,
  input  Operand_A,
  input  Carry_In,
  input  Binvert,
  input  [1:0] Operation,
  output Result0,
  output Carry0
);

  wire adder_1_out, and_1_out, multiplexer_1_out, not_1_out, or_1_out;

  not not_1 (not_1_out, Operand_B);
  Multiplexer multiplexer_1 (.in0(Operand_B), .in1(not_1_out), .out(multiplexer_1_out), .sel(Binvert));  // open: en
  and and_1 (and_1_out, Operand_A, multiplexer_1_out);
  or or_1 (or_1_out, Operand_A, multiplexer_1_out);
  Adder #(.width(1)) adder_1 (.a(Operand_A), .b(multiplexer_1_out), .out(adder_1_out), .cin(Carry_In), .cout(Carry0));
  Multiplexer #(.select(2)) multiplexer_2 (
    .in0(and_1_out), .in1(or_1_out), .in2(adder_1_out), .out(Result0), .sel(Operation));  // open: in3, en
endmodule

module _16_bit_ALU (
  input  Carry_In,
  input  [15:0] Operand_A,
  input  [15:0] Operand_B,
  input  [1:0] Operation,
  input  Binvert,
  output zero,
  output [15:0] result,
  output Carry15,
  output Overflow
);

  wire n1_bit_alu_1_carry0, n1_bit_alu_2_carry0, n1_bit_alu_3_carry0, n1_bit_alu_4_carry0,
       n1_bit_alu_5_carry0, n1_bit_alu_6_carry0, n1_bit_alu_7_carry0, n1_bit_alu_8_carry0,
       n1_bit_alu_9_carry0, n1_bit_alu_10_carry0, n1_bit_alu_11_carry0, n1_bit_alu_12_carry0,
       n1_bit_alu_13_carry0, n1_bit_alu_14_carry0, n1_bit_alu_15_carry0;

  _1_Bit_ALU u_1_bit_alu_1 (
    .Result0(result[0]), .Carry0(n1_bit_alu_1_carry0), .Operand_B(Operand_B[0]), .Operand_A(Operand_A[0]),
    .Binvert(Binvert), .Operation(Operation), .Carry_In(Carry_In));
  _1_Bit_ALU u_1_bit_alu_2 (
    .Result0(result[1]), .Carry0(n1_bit_alu_2_carry0), .Operand_B(Operand_B[1]), .Operand_A(Operand_A[1]),
    .Binvert(Binvert), .Operation(Operation), .Carry_In(n1_bit_alu_1_carry0));
  _1_Bit_ALU u_1_bit_alu_3 (
    .Result0(result[2]), .Carry0(n1_bit_alu_3_carry0), .Operand_B(Operand_B[2]), .Operand_A(Operand_A[2]),
    .Binvert(Binvert), .Operation(Operation), .Carry_In(n1_bit_alu_2_carry0));
  _1_Bit_ALU u_1_bit_alu_4 (
    .Result0(result[3]), .Carry0(n1_bit_alu_4_carry0), .Operand_B(Operand_B[3]), .Operand_A(Operand_A[3]),
    .Binvert(Binvert), .Operation(Operation), .Carry_In(n1_bit_alu_3_carry0));
  _1_Bit_ALU u_1_bit_alu_5 (
    .Result0(result[4]), .Carry0(n1_bit_alu_5_carry0), .Operand_B(Operand_B[4]), .Operand_A(Operand_A[4]),
    .Binvert(Binvert), .Operation(Operation), .Carry_In(n1_bit_alu_4_carry0));
  _1_Bit_ALU u_1_bit_alu_6 (
    .Result0(result[5]), .Carry0(n1_bit_alu_6_carry0), .Operand_B(Operand_B[5]), .Operand_A(Operand_A[5]),
    .Binvert(Binvert), .Operation(Operation), .Carry_In(n1_bit_alu_5_carry0));
  _1_Bit_ALU u_1_bit_alu_7 (
    .Result0(result[6]), .Carry0(n1_bit_alu_7_carry0), .Operand_B(Operand_B[6]), .Operand_A(Operand_A[6]),
    .Binvert(Binvert), .Operation(Operation), .Carry_In(n1_bit_alu_6_carry0));
  _1_Bit_ALU u_1_bit_alu_8 (
    .Result0(result[7]), .Carry0(n1_bit_alu_8_carry0), .Operand_B(Operand_B[7]), .Operand_A(Operand_A[7]),
    .Binvert(Binvert), .Operation(Operation), .Carry_In(n1_bit_alu_7_carry0));
  _1_Bit_ALU u_1_bit_alu_9 (
    .Result0(result[8]), .Carry0(n1_bit_alu_9_carry0), .Operand_B(Operand_B[8]), .Operand_A(Operand_A[8]),
    .Binvert(Binvert), .Operation(Operation), .Carry_In(n1_bit_alu_8_carry0));
  _1_Bit_ALU u_1_bit_alu_10 (
    .Result0(result[9]), .Carry0(n1_bit_alu_10_carry0), .Operand_B(Operand_B[9]), .Operand_A(Operand_A[9]),
    .Binvert(Binvert), .Operation(Operation), .Carry_In(n1_bit_alu_9_carry0));
  _1_Bit_ALU u_1_bit_alu_11 (
    .Result0(result[10]), .Carry0(n1_bit_alu_11_carry0), .Operand_B(Operand_B[10]),
    .Operand_A(Operand_A[10]), .Binvert(Binvert), .Operation(Operation), .Carry_In(n1_bit_alu_10_carry0));
  _1_Bit_ALU u_1_bit_alu_12 (
    .Result0(result[11]), .Carry0(n1_bit_alu_12_carry0), .Operand_B(Operand_B[11]),
    .Operand_A(Operand_A[11]), .Binvert(Binvert), .Operation(Operation), .Carry_In(n1_bit_alu_11_carry0));
  _1_Bit_ALU u_1_bit_alu_13 (
    .Result0(result[12]), .Carry0(n1_bit_alu_13_carry0), .Operand_B(Operand_B[12]),
    .Operand_A(Operand_A[12]), .Binvert(Binvert), .Operation(Operation), .Carry_In(n1_bit_alu_12_carry0));
  _1_Bit_ALU u_1_bit_alu_14 (
    .Result0(result[13]), .Carry0(n1_bit_alu_14_carry0), .Operand_B(Operand_B[13]),
    .Operand_A(Operand_A[13]), .Binvert(Binvert), .Operation(Operation), .Carry_In(n1_bit_alu_13_carry0));
  _1_Bit_ALU u_1_bit_alu_15 (
    .Result0(result[14]), .Carry0(n1_bit_alu_15_carry0), .Operand_B(Operand_B[14]),
    .Operand_A(Operand_A[14]), .Binvert(Binvert), .Operation(Operation), .Carry_In(n1_bit_alu_14_carry0));
  _1_Bit_ALU u_1_bit_alu_16 (
    .Result0(result[15]), .Carry0(Carry15), .Operand_B(Operand_B[15]), .Operand_A(Operand_A[15]),
    .Binvert(Binvert), .Operation(Operation), .Carry_In(n1_bit_alu_15_carry0));
  xor xor_1 (Overflow, n1_bit_alu_15_carry0, Carry15);
  nor nor_1 (zero, result[0], result[1], result[2], result[3], result[4], result[5], result[6], result[7], result[8], result[9], result[10], result[11], result[12], result[13], result[14], result[15]);

  // Other names for the same wires on the sheet: A0 = Operand_A[0]; A1 = Operand_A[1]; A2 = Operand_A[2];
  //   A3 = Operand_A[3]; A4 = Operand_A[4]; A5 = Operand_A[5]; A6 = Operand_A[6]; A7 = Operand_A[7];
  //   A8 = Operand_A[8]; A9 = Operand_A[9]; A10 = Operand_A[10]; A11 = Operand_A[11]; A12 = Operand_A[12];
  //   A13 = Operand_A[13]; A14 = Operand_A[14]; A15 = Operand_A[15]; B0 = Operand_B[0]; B1 = Operand_B[1];
  //   B2 = Operand_B[2]; B3 = Operand_B[3]; B4 = Operand_B[4]; B5 = Operand_B[5]; B6 = Operand_B[6];
  //   B7 = Operand_B[7]; B8 = Operand_B[8]; B9 = Operand_B[9]; B10 = Operand_B[10]; B11 = Operand_B[11];
  //   B12 = Operand_B[12]; B13 = Operand_B[13]; B14 = Operand_B[14]; B15 = Operand_B[15]
endmodule
