// Logisim project Final 16-bit cpu design.circ as structural Verilog: 22 circuits, main circuit main
module main (
  output SIGN,
  output CARRY,
  output [15:0] AR,
  output ZERO,
  output Parity,
  output [15:0] PC,
  output [15:0] DR,
  output [15:0] AC,
  output [15:0] IR
);

  wire Clear_Ram_out, Clear_Registers_out, control_logic_1_clk, control_logic_1_ld, control_logic_1_sel,
       control_logic_1_str, Start_out;
  wire [11:0] control_logic_1_address;
  wire [15:0] control_logic_1_datain, ram_1_data;

  Button Start (.out(Start_out));
  Button Clear_Registers (.out(Clear_Registers_out));
  Control_logic control_logic_1 (
    .Sign_Flag(SIGN), .Carry_Flag(CARRY), .Zero_Flag(ZERO), .Parity_Flag(Parity), .Str(control_logic_1_str),
    .Sel(control_logic_1_sel), .CLK(control_logic_1_clk), .ld(control_logic_1_ld), .DATAout(ram_1_data),
    .Address(control_logic_1_address), .DATAin(control_logic_1_datain), .START(Start_out),
    .clr_reg(Clear_Registers_out), .AR(AR), .PC(PC), .DR(DR), .AC(AC), .IR(IR));  // open: clr
  RAM #(.addrWidth(12), .dataWidth(16), .bus("separate")) ram_1 (
    .addr(control_logic_1_address), .din(control_logic_1_datain), .data(ram_1_data),
    .str(control_logic_1_str), .sel(control_logic_1_sel), .clk(control_logic_1_clk), .ld(control_logic_1_ld),
    .clr(Clear_Ram_out));
  Button Clear_Ram (.out(Clear_Ram_out));
  Hex_Digit_Display hex_digit_display_1 (.value(DR[15:12]));  // open: dp
  Hex_Digit_Display hex_digit_display_2 (.value(AC[15:12]));  // open: dp
  Hex_Digit_Display hex_digit_display_3 (.value(DR[11:8]));  // open: dp
  Hex_Digit_Display hex_digit_display_4 (.value(AC[11:8]));  // open: dp
  Hex_Digit_Display hex_digit_display_5 (.value(DR[3:0]));  // open: dp
  Hex_Digit_Display hex_digit_display_6 (.value(DR[7:4]));  // open: dp
  Hex_Digit_Display hex_digit_display_7 (.value(AC[3:0]));  // open: dp
  Hex_Digit_Display hex_digit_display_8 (.value(AC[7:4]));  // open: dp

  // Notes on the sheet:
  //   Nirmal Lunagariya 20BEC024
  //   Dev Desai 20BEC026
  //   Dhyey Kasundra 20BEC043
  //   Vatsa Kala 20BEC046
endmodule

// 16-REG
module REGISTER_16BIT (
  input  [15:0] IN,
  input  CLK,
  input  CLR,
  input  INC,
  input  LD,
  output [15:0] OUT
);

  wire or_1_out;
  wire [15:0] adder_1_out, and_1_out, multiplexer_1_out, not_1_out;

  assign not_1_out = ~OUT;  // NOT_Gate not_1, 16 bits wide
  assign and_1_out = OUT & not_1_out;  // AND_Gate and_1, 16 bits wide
  Adder #(.width(16)) adder_1 (.a(OUT), .b(and_1_out), .out(adder_1_out), .cin(1'b1));  // open: cout
  or or_1 (or_1_out, LD, INC);
  Multiplexer #(.width(16)) multiplexer_1 (.in0(IN), .in1(adder_1_out), .out(multiplexer_1_out), .sel(INC), .en(1'b1));
  Register #(.width(16)) register_1 (.D(multiplexer_1_out), .en(or_1_out), .Q(OUT), .clk(CLK), .clr(CLR));

  // Notes on the sheet:
  //   Nirmal Lunagariya 20BEC024
  //   Dev Desai 20BEC026
  //   Dhyey Kasundra 20BEC043
  //   Vatsa Kala 20BEC046
endmodule

// 12-REG
module REGISTER_12BIT (
  input  [15:0] IN,
  input  CLK,
  input  CLR,
  input  INC,
  input  LD,
  output [15:0] OUT
);

  wire or_1_out;
  wire [11:0] adder_1_out, and_1_out, multiplexer_1_out, not_1_out;

  assign not_1_out = ~OUT[11:0];  // NOT_Gate not_1, 12 bits wide
  assign and_1_out = OUT[11:0] & not_1_out;  // AND_Gate and_1, 12 bits wide
  Adder #(.width(12)) adder_1 (.a(OUT[11:0]), .b(and_1_out), .out(adder_1_out), .cin(1'b1));  // open: cout
  or or_1 (or_1_out, LD, INC);
  Multiplexer #(.width(12)) multiplexer_1 (
    .in0(IN[11:0]), .in1(adder_1_out), .out(multiplexer_1_out), .sel(INC), .en(1'b1));
  Register #(.width(12)) register_1 (.D(multiplexer_1_out), .en(or_1_out), .Q(OUT[11:0]), .clk(CLK), .clr(CLR));

  assign OUT[15:12] = 4'b0000;

  // Notes on the sheet:
  //   Dikshant - 20BIT036
  //   Nirmal Lunagariya 20BEC024
  //   Dev Desai 20BEC026
  //   Dhyey Kasundra 20BEC043
  //   Vatsa Kala 20BEC046
endmodule

module AU16 (
  input  [1:0] SELECT,
  input  Cin,
  input  [15:0] A,
  input  [15:0] B,
  input  EN,
  output [15:0] OUT,
  output E
);

  wire adder_1_cout;
  wire [15:0] multiplexer_1_out, not_1_out;

  assign not_1_out = ~B;  // NOT_Gate not_1, 16 bits wide
  Multiplexer #(.select(2), .width(16)) multiplexer_1 (
    .in0(B), .in1(not_1_out), .in2({16{1'b0}}), .in3({16{1'b1}}), .out(multiplexer_1_out), .sel(SELECT),
    .en(EN));
  Adder #(.width(16)) adder_1 (.a(A), .b(multiplexer_1_out), .out(OUT), .cin(Cin), .cout(adder_1_cout));
  xor xor_1 (E, adder_1_cout, Cin);

  // Notes on the sheet:
  //   Nirmal Lunagariya 20BEC024
  //   Dev Desai 20BEC026
  //   Dhyey Kasundra 20BEC043
  //   Vatsa Kala 20BEC046
endmodule

module LU16 (
  input  [15:0] A,
  input  [1:0] SELECT,
  input  [15:0] B,
  input  ENABLE,
  output [15:0] OUT
);

  wire [15:0] and_1_out, not_1_out, or_1_out, xor_1_out;

  assign not_1_out = ~A;  // NOT_Gate not_1, 16 bits wide
  assign and_1_out = A & B;  // AND_Gate and_1, 16 bits wide
  assign or_1_out = A | B;  // OR_Gate or_1, 16 bits wide
  assign xor_1_out = A ^ B;  // XOR_Gate xor_1, 16 bits wide
  Multiplexer #(.select(2), .width(16)) multiplexer_1 (
    .in0(and_1_out), .in1(or_1_out), .in2(xor_1_out), .in3(not_1_out), .out(OUT), .sel(SELECT), .en(ENABLE));

  // Notes on the sheet:
  //   Dev Desai 20BEC026
  //   Vatsa Kala 20BEC046
  //   Nirmal Lunagariya 20BEC024
  //   Dhyey Kasundra 20BEC043
endmodule

module SU16 (
  input  [15:0] in_1,
  input  in_2,
  output ER,
  output EL,
  output [15:0] SHR,
  output [15:0] SHL
);


  assign EL = in_1[15];
  assign ER = in_1[0];
  assign SHL = {in_1[14:0], in_2};
  assign SHR = {in_2, in_1[15:1]};

  // Notes on the sheet:
  //   Nirmal Lunagariya 20BEC024
  //   Dev Desai 20BEC026
  //   Dhyey Kasundra 20BEC043
  //   Vatsa Kala 20BEC046
endmodule

// ALU16
module ALU_16BIT (
  input  [3:0] SELECT,
  input  Cin,
  input  Clr_E,
  input  [15:0] A,
  input  [15:0] B,
  input  ALU_EN,
  input  Clk,
  input  Clr_E_2,
  output [15:0] OUT,
  output E
);

  wire au16_1_e, controlled_buffer_1_out, controlled_buffer_3_out, d_ff_1_qn, multiplexer_2_out, not_1_out,
       su16_1_el, su16_1_er;
  wire [15:0] au16_1_out, lu16_1_out, su16_1_shl, su16_1_shr;

  AU16 au16_1 (.A(A), .B(B), .SELECT(SELECT[1:0]), .Cin(Cin), .EN(1'b1), .OUT(au16_1_out), .E(au16_1_e));
  LU16 lu16_1 (.A(A), .B(B), .SELECT(SELECT[1:0]), .ENABLE(1'b1), .OUT(lu16_1_out));
  SU16 su16_1 (.in_1(A), .ER(su16_1_er), .EL(su16_1_el), .in_2(E), .SHR(su16_1_shr), .SHL(su16_1_shl));
  Multiplexer #(.select(2), .width(16)) multiplexer_1 (
    .in0(au16_1_out), .in1(lu16_1_out), .in2(su16_1_shr), .in3(su16_1_shl), .out(OUT), .sel(SELECT[3:2]),
    .en(1'b1));
  Multiplexer #(.select(2)) multiplexer_2 (
    .in0(au16_1_e), .in1(1'b0), .in2(su16_1_er), .in3(su16_1_el), .out(multiplexer_2_out), .sel(SELECT[3:2]),
    .en(1'b1));
  assign controlled_buffer_1_out = not_1_out ? controlled_buffer_3_out : 1'bz;  // Controlled_Buffer controlled_buffer_1
  assign controlled_buffer_1_out = ALU_EN ? multiplexer_2_out : 1'bz;  // Controlled_Buffer controlled_buffer_2
  not not_1 (not_1_out, ALU_EN);
  assign controlled_buffer_3_out = Clr_E ? d_ff_1_qn : 1'bz;  // Controlled_Buffer controlled_buffer_3
  D_Flip_Flop d_ff_1 (
    .clk(Clk), .D(controlled_buffer_1_out), .Q(E), .Qn(d_ff_1_qn), .reset(Clr_E_2));  // open: preset, en

  // Notes on the sheet:
  //   Nirmal Lunagariya 20BEC024
  //   Dev Desai 20BEC026
  //   Dhyey Kasundra 20BEC043
  //   Vatsa Kala 20BEC046
endmodule

// P_F
module Parity_Flag (
  input  [15:0] AC,
  output FLAG
);

  wire xor_1_out, xor_2_out, xor_3_out, xor_4_out, xor_5_out, xor_6_out, xor_7_out, xor_8_out, xor_9_out,
       xor_10_out, xor_11_out, xor_12_out, xor_13_out, xor_14_out, xor_15_out;

  xor xor_1 (xor_1_out, AC[0], AC[1]);
  xor xor_2 (xor_2_out, AC[2], AC[3]);
  xor xor_3 (xor_3_out, AC[4], AC[5]);
  xor xor_4 (xor_4_out, AC[6], AC[7]);
  xor xor_5 (xor_5_out, AC[8], AC[9]);
  xor xor_6 (xor_6_out, AC[10], AC[11]);
  xor xor_7 (xor_7_out, AC[12], AC[13]);
  xor xor_8 (xor_8_out, AC[14], AC[15]);
  xor xor_9 (xor_9_out, xor_1_out, xor_2_out);
  xor xor_10 (xor_10_out, xor_3_out, xor_4_out);
  xor xor_11 (xor_11_out, xor_5_out, xor_6_out);
  xor xor_12 (xor_12_out, xor_7_out, xor_8_out);
  xor xor_13 (xor_13_out, xor_9_out, xor_10_out);
  xor xor_14 (xor_14_out, xor_11_out, xor_12_out);
  xor xor_15 (xor_15_out, xor_13_out, xor_14_out);
  not not_1 (FLAG, xor_15_out);

  // Notes on the sheet:
  //   Dev Desai 20BEC026
  //   Vatsa Kala 20BEC046
  //   Nirmal Lunagariya 20BEC024
  //   Dhyey Kasundra 20BEC043
endmodule

// CONTROL UNIT
module Control_Unit (
  input  [15:0] IR,
  input  EN_Counter,
  input  CLR_Counter,
  input  CLK,
  output [11:0] Address,
  output D0,
  output D1,
  output D2,
  output D3,
  output D4,
  output D5,
  output D6,
  output D7,
  output I,
  output T0,
  output T1,
  output T2,
  output T3,
  output T4,
  output T5,
  output T6,
  output T7,
  output T8,
  output T9,
  output T10,
  output T11,
  output T12,
  output T13,
  output T14,
  output T15
);

  wire [3:0] counter_1_q;

  Counter #(.width(4), .max('hf)) counter_1 (
    .count(EN_Counter), .Q(counter_1_q), .clk(CLK), .clr(T7));  // open: load, D, carry
  Decoder #(.select(3)) decoder_1 (
    .out0(D0), .out1(D1), .out2(D2), .out3(D3), .out4(D4), .out5(D5), .out6(D6), .out7(D7), .sel(IR[14:12]),
    .en(EN_Counter));
  Decoder #(.select(4)) decoder_2 (
    .out0(T0), .out1(T1), .out2(T2), .out3(T3), .out4(T4), .out5(T5), .out6(T6), .out7(T7), .out8(T8),
    .out9(T9), .out10(T10), .out11(T11), .out12(T12), .out13(T13), .out14(T14), .out15(T15),
    .sel(counter_1_q), .en(EN_Counter));

  assign Address = IR[11:0];
  assign I = IR[15];

  // Notes on the sheet:
  //   Nirmal Lunagariya 20BEC024
  //   Dev Desai 20BEC026
  //   Dhyey Kasundra 20BEC043
  //   Vatsa Kala 20BEC046
endmodule

// AR_L
module AR_Logic (
  input  D5,
  input  D7,
  input  I,
  input  T0,
  input  T2,
  input  T3,
  input  T4,
  output LD,
  output INC,
  output CLR
);

  wire and_1_out, not_1_out;

  not not_1 (not_1_out, D7);
  and and_1 (and_1_out, not_1_out, I, T3);
  or or_1 (LD, and_1_out, T2, T0);
  and and_2 (INC, D5, T4);

  assign CLR = 1'b0;

  // Notes on the sheet:
  //   Dev Desai 20BEC026
  //   Vatsa Kala 20BEC046
  //   Nirmal Lunagariya 20BEC024
  //   Dhyey Kasundra 20BEC043
endmodule

// AC_L
module AC_Logic (
  input  B5,
  input  B6,
  input  B7,
  input  B9,
  input  B11,
  input  D0,
  input  D1,
  input  D2,
  input  D7,
  input  I,
  input  T3,
  input  T4,
  input  T5,
  output LD,
  output INC,
  output CLR
);

  wire and_1_out, and_2_out, and_3_out, and_4_out, and_6_out, not_1_out, or_1_out, or_2_out;

  or or_1 (or_1_out, B6, B7, B9);
  not not_1 (not_1_out, I);
  or or_2 (or_2_out, D0, D1, D2);
  and and_1 (and_1_out, D7, not_1_out, T3);
  and and_2 (and_2_out, or_2_out, T5);
  and and_3 (and_3_out, or_1_out, and_1_out);
  or or_3 (LD, and_2_out, and_3_out);
  and and_4 (and_4_out, D2, T4);
  and and_5 (INC, B5, and_1_out);
  and and_6 (and_6_out, B11, and_1_out);
  or or_4 (CLR, and_6_out, and_4_out);

  // Notes on the sheet:
  //   Dev Desai 20BEC026
  //   Vatsa Kala 20BEC046
  //   Nirmal Lunagariya 20BEC024
  //   Dhyey Kasundra 20BEC043
endmodule

// PC_L
module PC_Logic (
  input  B1,
  input  B2,
  input  B3,
  input  B4,
  input  D4,
  input  D5,
  input  D6,
  input  D7,
  input  I,
  input  T1,
  input  T3,
  input  T4,
  input  T5,
  input  T6,
  input  E,
  input  [15:0] DR,
  input  [15:0] AC,
  output LD,
  output INC,
  output CLR
);

  wire and_1_out, and_2_out, and_3_out, and_4_out, and_5_out, and_6_out, and_7_out, and_8_out, and_9_out,
       not_1_out, not_2_out, not_3_out, not_4_out, not_5_out, or_1_out, or_2_out, or_3_out;

  not not_1 (not_1_out, or_1_out);
  or or_1 (or_1_out, DR[15], DR[14], DR[13], DR[12], DR[11], DR[10], DR[9], DR[8], DR[6], DR[5], DR[4], DR[3], DR[2], DR[1], DR[0], DR[7]);
  not not_2 (not_2_out, I);
  and and_1 (and_1_out, D7, not_2_out, T3);
  not not_3 (not_3_out, or_2_out);
  or or_2 (or_2_out, AC[15], AC[14], AC[13], AC[12], AC[11], AC[10], AC[9], AC[8], AC[6], AC[5], AC[4], AC[3], AC[2], AC[1], AC[0], AC[7]);
  not not_4 (not_4_out, AC[15]);
  and and_2 (and_2_out, B1, not_5_out);
  and and_3 (and_3_out, B2, not_3_out);
  and and_4 (and_4_out, B3, AC[15]);
  and and_5 (and_5_out, B4, not_4_out);
  not not_5 (not_5_out, E);
  and and_6 (and_6_out, D4, T4);
  and and_7 (and_7_out, D5, T5);
  or or_3 (or_3_out, and_2_out, and_3_out, and_4_out, and_5_out);
  and and_8 (and_8_out, or_3_out, and_1_out);
  or or_4 (LD, and_6_out, and_7_out);
  and and_9 (and_9_out, not_1_out, D6, T6);
  or or_5 (INC, and_8_out, and_9_out, T1);

  assign CLR = 1'b0;

  // Notes on the sheet:
  //   Dev Desai 20BEC026
  //   Vatsa Kala 20BEC046
  //   Nirmal Lunagariya 20BEC024
  //   Dhyey Kasundra 20BEC043
endmodule

// IR_L
module IR_Logic (
  input  T1,
  output LD
);


  assign LD = T1;

  // Notes on the sheet:
  //   Nirmal Lunagariya 20BEC024
  //   Dev Desai 20BEC026
  //   Dhyey Kasundra 20BEC043
  //   Vatsa Kala 20BEC046
endmodule

// DR_L
module DR_Logic (
  input  D0,
  input  D1,
  input  D2,
  input  D6,
  input  T4,
  input  T5,
  output LD,
  output INC,
  output CLR
);

  wire or_1_out;

  or or_1 (or_1_out, D0, D1, D2, D6);
  and and_1 (INC, D6, T5);
  and and_2 (LD, or_1_out, T4);

  assign CLR = 1'b0;

  // Notes on the sheet:
  //   Dev Desai 20BEC026
  //   Vatsa Kala 20BEC046
  //   Nirmal Lunagariya 20BEC024
  //   Dhyey Kasundra 20BEC043
endmodule

// MEM_L
module MEM_Logic (
  input  D3,
  input  D5,
  input  D6,
  input  T4,
  input  T6,
  output LD
);

  wire and_1_out, and_2_out, or_1_out;

  or or_1 (or_1_out, D3, D5);
  and and_1 (and_1_out, or_1_out, T4);
  and and_2 (and_2_out, D6, T6);
  or or_2 (LD, and_1_out, and_2_out);

  // Notes on the sheet:
  //   Nirmal Lunagariya 20BEC024
  //   Dev Desai 20BEC026
  //   Dhyey Kasundra 20BEC043
  //   Vatsa Kala 20BEC046
endmodule

// BUS_L
module BUS_Logic (
  input  D7,
  input  D6,
  input  D5,
  input  D4,
  input  D3,
  input  D2,
  input  D1,
  input  D0,
  input  I,
  input  T0,
  input  T1,
  input  T2,
  input  T3,
  input  T4,
  input  T5,
  input  T6,
  output [2:0] Select
);

  wire and_1_out, and_2_out, and_3_out, and_4_out, and_5_out, and_6_out, and_7_out, not_1_out, or_1_out,
       or_2_out, or_3_out;

  not not_1 (not_1_out, D7);
  and and_1 (and_1_out, not_1_out, I, T3);
  or or_1 (or_1_out, D6, D2, D1, D0);
  and and_2 (and_2_out, or_1_out, T4);
  or or_2 (or_2_out, and_1_out, T1, and_2_out);
  and and_3 (and_3_out, D3, T4);
  and and_4 (and_4_out, D4, T4);
  and and_5 (and_5_out, D5, T5);
  and and_6 (and_6_out, D6, T6);
  or or_3 (or_3_out, and_3_out, or_2_out);
  and and_7 (and_7_out, T4, D5);
  or or_4 (Select[2], or_3_out, T2);
  or or_5 (Select[0], and_4_out, and_5_out, T2, and_6_out, or_2_out);
  or or_6 (Select[1], T0, or_2_out, and_7_out);

  // Notes on the sheet:
  //   Nirmal Lunagariya 20BEC024
  //   Dev Desai 20BEC026
  //   Dhyey Kasundra 20BEC043
  //   Vatsa Kala 20BEC046
endmodule

// ALU_L
module ALU_Logic (
  input  B6,
  input  B7,
  input  B9,
  input  D0,
  input  D7,
  input  I,
  input  T3,
  input  T5,
  output [3:0] Select,
  output Cin
);

  wire and_1_out, and_2_out, and_3_out, and_4_out, not_1_out;

  not not_1 (not_1_out, I);
  and and_1 (and_1_out, D0, T5);
  and and_2 (and_2_out, D7, T3, not_1_out);
  and and_3 (and_3_out, B7, and_2_out);
  and and_4 (and_4_out, and_2_out, B6);
  and and_5 (Select[1], and_2_out, B9);
  or or_1 (Select[3], and_3_out, and_4_out);
  or or_2 (Select[2], Select[1], and_1_out, and_4_out);

  assign Cin = 1'b0;
  assign Select[0] = Select[1];

  // Notes on the sheet:
  //   Nirmal Lunagariya 20BEC024
  //   Dev Desai 20BEC026
  //   Dhyey Kasundra 20BEC043
  //   Vatsa Kala 20BEC046
endmodule

// CB
module CommonBus (
  input  EN_DEC,
  input  [2:0] DEC_Select,
  input  [3:0] ALU_Select,
  input  Cin,
  input  [15:0] Dataout,
  input  LD_MEM,
  input  CLR_RAM,
  input  LD_AR,
  input  INC_AR,
  input  CLR_AR,
  input  LD_PC,
  input  INC_PC,
  input  CLR_PC,
  input  LD_DR,
  input  INC_DR,
  input  CLR_DR,
  input  LD_AC,
  input  INC_AC,
  input  CLR_AC,
  input  LD_IR,
  input  LD_TR,
  input  INC_TR,
  input  CLR_TR,
  input  Clr_register,
  input  Clr_E,
  input  CLK,
  input  Comp_E,
  output [11:0] Address,
  output [15:0] Datain,
  output Str,
  output CLK_2,
  output Sel,
  output [15:0] CBOUT,
  output ld,
  output clr,
  output [15:0] AR,
  output [15:0] PC,
  output [15:0] DR,
  output E,
  output [15:0] AC,
  output [15:0] IR,
  output [15:0] TR
);

  wire decoder_1_out0, decoder_1_out1, decoder_1_out2, decoder_1_out3, decoder_1_out4, decoder_1_out5,
       decoder_1_out6, or_1_out, or_2_out, or_3_out, or_4_out;
  wire [15:0] alu_16bit_1_out;

  or or_1 (or_1_out, CLR_RAM, CLR_AR);
  or or_2 (or_2_out, CLR_RAM, CLR_PC);
  or or_3 (or_3_out, Clr_register, CLR_DR);
  or or_4 (or_4_out, Clr_register, CLR_AC);
  or or_5 (Sel, LD_MEM, ld);
  ALU_16BIT alu_16bit_1 (
    .A(AC), .B(DR), .Cin(Cin), .SELECT(ALU_Select), .Clr_E(Comp_E), .ALU_EN(LD_AC), .Clk(CLK),
    .Clr_E_2(Clr_E), .OUT(alu_16bit_1_out), .E(E));
  REGISTER_12BIT u_AR (.IN(Dataout), .LD(LD_AR), .INC(INC_AR), .CLR(or_1_out), .CLK(CLK), .OUT({AR[15:12], Address}));
  REGISTER_12BIT u_PC (.IN(Dataout), .LD(LD_PC), .INC(INC_PC), .CLR(or_2_out), .CLK(CLK), .OUT(PC));
  REGISTER_16BIT u_DR (.IN(Dataout), .LD(LD_DR), .INC(INC_DR), .CLR(or_3_out), .CLK(CLK), .OUT(DR));
  REGISTER_16BIT u_AC (.IN(alu_16bit_1_out), .LD(LD_AC), .INC(INC_AC), .CLR(or_4_out), .CLK(CLK), .OUT(AC));
  REGISTER_16BIT u_IR (.IN(Dataout), .LD(LD_IR), .INC(1'b0), .CLR(CLR_RAM), .CLK(CLK), .OUT(IR));
  REGISTER_16BIT u_TR (.IN(Dataout), .LD(LD_TR), .INC(INC_TR), .CLR(CLR_TR), .CLK(CLK), .OUT(TR));
  Decoder #(.select(3)) decoder_1 (
    .out0(decoder_1_out0), .out1(decoder_1_out1), .out2(decoder_1_out2), .out3(decoder_1_out3),
    .out4(decoder_1_out4), .out5(decoder_1_out5), .out6(decoder_1_out6), .out7(ld), .sel(DEC_Select),
    .en(EN_DEC));
  assign Dataout = decoder_1_out0 ? {16{1'b0}} : 16'bz;  // Controlled_Buffer controlled_buffer_1
  assign Dataout = decoder_1_out1 ? {AR[15:12], Address} : 16'bz;  // Controlled_Buffer controlled_buffer_2
  assign Dataout = decoder_1_out2 ? PC : 16'bz;  // Controlled_Buffer controlled_buffer_3
  assign Dataout = decoder_1_out3 ? DR : 16'bz;  // Controlled_Buffer controlled_buffer_4
  assign Dataout = decoder_1_out4 ? AC : 16'bz;  // Controlled_Buffer controlled_buffer_5
  assign Dataout = decoder_1_out5 ? IR : 16'bz;  // Controlled_Buffer controlled_buffer_6
  assign Dataout = decoder_1_out6 ? TR : 16'bz;  // Controlled_Buffer controlled_buffer_7

  assign AR[11:0] = Address;
  assign CBOUT = Dataout;
  assign CLK_2 = CLK;
  assign clr = CLR_RAM;
  assign Datain = Dataout;
  assign Str = LD_MEM;

  // Notes on the sheet:
  //   Nirmal Lunagariya 20BEC024
  //   Dev Desai 20BEC026
  //   Dhyey Kasundra 20BEC043
  //   Vatsa Kala 20BEC046
endmodule

// CT_L
module Counter_L (
  input  I,
  input  T3,
  input  T4,
  input  T5,
  input  T6,
  input  D0,
  input  D1,
  input  D2,
  input  D3,
  input  D4,
  input  D5,
  input  D6,
  input  D7,
  output CLR
);

  wire and_1_out, and_2_out, and_3_out, and_4_out, not_1_out, or_1_out, or_2_out;

  or or_1 (or_1_out, D3, D4);
  not not_1 (not_1_out, I);
  or or_2 (or_2_out, D0, D1, D2, D5);
  and and_1 (and_1_out, T3, not_1_out, D7);
  and and_2 (and_2_out, T5, or_2_out);
  and and_3 (and_3_out, T4, or_1_out);
  and and_4 (and_4_out, T6, D6);
  or or_3 (CLR, and_2_out, and_4_out, and_3_out, and_1_out);

  // Notes on the sheet:
  //   Dev Desai 20BEC026
  //   Nirmal Lunagariya 20BEC024
  //   Dhyey Kasundra 20BEC043
  //   Vatsa Kala 20BEC046
endmodule

module HLT (
  input  B0,
  input  D7,
  input  I,
  input  T3,
  output STOP
);

  wire not_1_out;

  not not_1 (not_1_out, I);
  and and_1 (STOP, B0, D7, not_1_out, T3);

  // Notes on the sheet:
  //   Dev Desai 20BEC026
  //   Vatsa Kala 20BEC046
  //   Nirmal Lunagariya 20BEC024
  //   Dhyey Kasundra 20BEC043
endmodule

// E_L
module E_Logic (
  input  B8,
  input  B10,
  input  D7,
  input  I,
  input  T3,
  output Clr_E,
  output Comp_E
);

  wire and_1_out, not_1_out;

  not not_1 (not_1_out, I);
  and and_1 (and_1_out, D7, not_1_out, T3);
  and and_2 (Clr_E, B10, and_1_out);
  and and_3 (Comp_E, and_1_out, B8);

  // Notes on the sheet:
  //   Dev Desai 20BEC026
  //   Vatsa Kala 20BEC046
  //   Nirmal Lunagariya 20BEC024
  //   Dhyey Kasundra 20BEC043
endmodule

// CPU
module Control_logic (
  input  [15:0] DATAout,
  input  START,
  input  clr_reg,
  output Str,
  output Sel,
  output CLK,
  output ld,
  output clr,
  output [11:0] Address,
  output [15:0] DATAin,
  output [15:0] AR,
  output [15:0] PC,
  output [15:0] DR,
  output [15:0] AC,
  output [15:0] IR,
  output Sign_Flag,
  output Carry_Flag,
  output Zero_Flag,
  output Parity_Flag
);

  wire B0, B1, B2, B3, B4, B5, B6, B7, B8, B9, B10, B11, Cin, CLK_t, clock_1_out, CLR_AC, CLR_AR,
       CLR_Counter, CLR_DR, CLR_E, CLR_PC, COMP_E, D0, D1, D2, D3, D4, D5, D6, D7, I, INC_AC, INC_AR, INC_DR,
       INC_PC, LD_AC, LD_AR, LD_DR, LD_IR, LD_MEM, LD_PC, or_1_out, or_2_out, register_1_q, STOP, T0, T1, T2,
       T3, T4, T5, T6, T7;
  wire [2:0] B_SELECT;
  wire [3:0] A_SELECT;

  Register #(.width(1)) register_1 (.D(START), .en(1'b1), .Q(register_1_q), .clk(START), .clr(STOP));
  assign CLK_t = register_1_q ? clock_1_out : 1'bz;  // Controlled_Buffer controlled_buffer_1
  Clock clock_1 (.out(clock_1_out));
  Control_Unit control_unit_1 (
    .IR(IR), .EN_Counter(register_1_q), .CLR_Counter(CLR_Counter), .CLK(CLK_t),
    .Address({B11, B10, B9, B8, B7, B6, B5, B4, B3, B2, B1, B0}), .D0(D0), .D1(D1), .D2(D2), .D3(D3),
    .D4(D4), .D5(D5), .D6(D6), .D7(D7), .I(I), .T0(T0), .T1(T1), .T2(T2), .T3(T3), .T4(T4), .T5(T5), .T6(T6),
    .T7(T7));  // open: T8, T9, T10, T11, T12, T13, T14, T15
  IR_Logic ir_logic_1 (.T1(T1), .LD(LD_IR));
  AR_Logic ar_logic_1 (
    .D5(D5), .D7(D7), .I(I), .T0(T0), .T2(T2), .T3(T3), .T4(T4), .LD(LD_AR), .INC(INC_AR), .CLR(CLR_AR));
  Counter_L counter_l_1 (
    .D0(D0), .D1(D1), .D2(D2), .D3(D3), .D4(D4), .D5(D5), .D6(D6), .D7(D7), .I(I), .T3(T3), .T4(T4), .T5(T5),
    .T6(T6), .CLR(CLR_Counter));
  ALU_Logic alu_logic_1 (
    .D0(D0), .D7(D7), .I(I), .T3(T3), .T5(T5), .B6(B6), .B7(B7), .B9(B9), .Select(A_SELECT), .Cin(Cin));
  AC_Logic ac_logic_1 (
    .B5(B5), .B6(B6), .B7(B7), .B9(B9), .B11(B11), .D0(D0), .D1(D1), .D2(D2), .D7(D7), .I(I), .T3(T1),
    .T4(T3), .T5(T6), .LD(LD_AC), .INC(INC_AC), .CLR(CLR_AC));
  BUS_Logic bus_logic_1 (
    .I(I), .T0(T0), .T1(T1), .T2(T2), .T3(T3), .T4(T4), .T5(T5), .T6(T6), .D7(D7), .D6(D2), .D5(D5), .D4(D4),
    .D3(D1), .D2(D6), .D1(D3), .D0(D0), .Select(B_SELECT));
  PC_Logic pc_logic_1 (
    .B1(B0), .B2(B1), .B3(B3), .B4(B4), .D4(D4), .D5(D5), .D6(D6), .D7(D7), .I(I), .T1(T1), .T3(T3), .T4(T4),
    .T5(T5), .T6(T6), .DR(DR), .AC(AC), .E(Carry_Flag), .LD(LD_PC), .INC(INC_PC), .CLR(CLR_PC));
  HLT hlt_1 (.B0(B0), .D7(D7), .I(I), .T3(T3), .STOP(STOP));
  MEM_Logic mem_logic_1 (.D3(D3), .D5(D5), .D6(D6), .T4(T4), .T6(T6), .LD(LD_MEM));
  not not_1 (Zero_Flag, or_1_out);
  E_Logic e_logic_1 (.D7(D7), .I(I), .T3(T3), .B8(B8), .B10(B10), .Clr_E(CLR_E), .Comp_E(COMP_E));
  or or_1 (or_1_out, AC[0], AC[1], AC[2], AC[3], AC[4], AC[5], AC[6], AC[7], AC[9], AC[10], AC[11], AC[12], AC[13], AC[14], AC[15], AC[8]);
  DR_Logic dr_logic_1 (.D0(D0), .D1(D1), .D2(D2), .D6(D6), .T4(T4), .T5(T5), .LD(LD_DR), .INC(INC_DR), .CLR(CLR_DR));
  Parity_Flag parity_flag_1 (.AC(AC), .FLAG(Parity_Flag));
  or or_2 (or_2_out, CLR_E, STOP);
  CommonBus commonbus_1 (
    .LD_MEM(LD_MEM), .LD_AR(LD_AR), .INC_AR(INC_AR), .CLR_AR(CLR_AR), .LD_PC(LD_PC), .INC_PC(INC_PC),
    .CLR_PC(CLR_PC), .LD_DR(LD_DR), .INC_DR(INC_DR), .CLR_DR(CLR_DR), .LD_AC(LD_AC), .INC_AC(INC_AC),
    .CLR_AC(CLR_AC), .LD_IR(LD_IR), .Str(Str), .Cin(Cin), .ALU_Select(A_SELECT), .Sel(Sel), .CLK_2(CLK),
    .ld(ld), .DEC_Select(B_SELECT), .EN_DEC(1'b1), .Address(Address), .clr(clr), .Datain(DATAin),
    .Dataout(DATAout), .Clr_register(clr_reg), .Comp_E(COMP_E), .CLK(CLK_t), .Clr_E(or_2_out),
    .CLR_RAM(STOP), .AR(AR), .PC(PC), .DR(DR), .E(Carry_Flag), .AC(AC), .IR(IR));  // open: LD_TR, INC_TR, CLR_TR, CBOUT, TR

  assign Sign_Flag = AC[15];

  // Other names for the same wires on the sheet: E = Carry_Flag

  // Notes on the sheet:
  //   Dev Desai 20BEC026
  //   Dhyey Kasundra 20BEC043
  //   Vatsa Kala 20BEC046
  //   Nirmal Lunagariya 20BEC024
endmodule
